// Digital circuit 08_full_adder.dig as structural Verilog
module _08_full_adder (
  input  P,
  input  Q,
  input  C_in,
  output S,
  output C_out
);

  wire _07_half_adder_1_c_out, _07_half_adder_1_s, _07_half_adder_2_c_out;

  _07_half_adder _07_half_adder_1 (.P(P), .Q(Q), .S(_07_half_adder_1_s), .C_out(_07_half_adder_1_c_out));
  _07_half_adder _07_half_adder_2 (.P(_07_half_adder_1_s), .Q(C_in), .S(S), .C_out(_07_half_adder_2_c_out));
  or or_1 (C_out, _07_half_adder_1_c_out, _07_half_adder_2_c_out);
endmodule
