// Digital circuit A1_2비트비교기.dig as structural Verilog
module \A1_2비트비교기  (
  input  A1,
  input  A0,
  input  B1,
  input  B0,
  output G,
  output L,
  output E
);

  wire and_1_out, and_2_out, and_3_out, and_4_out, and_5_out, and_6_out, not_1_out, not_2_out, xor_1_out,
       xor_2_out;

  xor xor_1 (xor_1_out, A1, B1);
  xor xor_2 (xor_2_out, A0, B0);
  not not_1 (not_1_out, xor_1_out);
  not not_2 (not_2_out, xor_2_out);
  and and_1 (and_1_out, xor_2_out, A0);
  and and_2 (and_2_out, xor_2_out, B0);
  and and_3 (and_3_out, xor_1_out, A1);
  and and_4 (and_4_out, xor_1_out, B1);
  and and_5 (and_5_out, not_1_out, and_1_out);
  and and_6 (and_6_out, not_1_out, and_2_out);
  or or_1 (G, and_3_out, and_5_out);
  or or_2 (L, and_4_out, and_6_out);
  and and_7 (E, not_1_out, not_2_out);
endmodule
