// Digital circuit A1_반가산기(HalfAdder)만들기.dig as structural Verilog
module \A1_반가산기_HalfAdder_만들기  (
  input  P,
  input  Q,
  output S,
  output C_out
);

  xor xor_1 (S, P, Q);
  and and_1 (C_out, P, Q);
endmodule
