// Digital circuit A2_2,3비트비교기.dig as structural Verilog
module \A2_2_3비트비교기  (
  input  A1,
  input  A0,
  input  B1,
  input  B0,
  input  B2,
  output G,
  output L,
  output E
);

  wire \a1_2비트비교기_1_e , \a1_2비트비교기_1_g , \a1_2비트비교기_1_l , and_1_out, not_1_out, not_2_out, not_3_out;

  \A1_2비트비교기  \a1_2비트비교기_1  (
    .A1(A1), .A0(A0), .B1(B1), .B0(B0), .G(\a1_2비트비교기_1_g ), .L(\a1_2비트비교기_1_l ), .E(\a1_2비트비교기_1_e ));
  not not_1 (not_1_out, B2);
  and and_1 (and_1_out, not_1_out, \a1_2비트비교기_1_l );
  and and_2 (G, not_2_out, \a1_2비트비교기_1_g );
  not not_2 (not_2_out, B2);
  and and_3 (E, not_3_out, \a1_2비트비교기_1_e );
  not not_3 (not_3_out, B2);
  or or_1 (L, and_1_out, B2);
endmodule
