// Digital circuit A2_전가산기(FullAdder)만들기.dig as structural Verilog
module \A2_전가산기_FullAdder_만들기  (
  input  P,
  input  Q,
  input  C_in,
  output S,
  output C_out
);

  wire \a1_반가산기_halfadder_만들기_1_c_out , \a1_반가산기_halfadder_만들기_1_s , and_1_out;

  \A1_반가산기_HalfAdder_만들기  \a1_반가산기_halfadder_만들기_1  (
    .P(P), .Q(Q), .S(\a1_반가산기_halfadder_만들기_1_s ), .C_out(\a1_반가산기_halfadder_만들기_1_c_out ));
  xor xor_1 (S, \a1_반가산기_halfadder_만들기_1_s , C_in);
  and and_1 (and_1_out, \a1_반가산기_halfadder_만들기_1_s , C_in);
  or or_1 (C_out, \a1_반가산기_halfadder_만들기_1_c_out , and_1_out);
endmodule
