// Digital circuit 15_seven_segment_yn.dig as structural Verilog
module _15_seven_segment_yn (
  input  Y,
  output a,
  output b,
  output c,
  output d,
  output e,
  output f,
  output g,
  output dp
);

  Seven_Seg seven_seg_1 ();  // open: a, b, c, d, e, f, g, dp
endmodule
