// Digital circuit 3번_입력이3개인AND게이트.dig as structural Verilog
module \_3번_입력이3개인AND게이트  (
  input  A,
  input  B,
  input  C,
  output Y
);

  wire and_1_out;

  and and_1 (and_1_out, A, B);
  and and_2 (Y, and_1_out, C);
endmodule
