// Digital circuit 4번_2대1멀티플렉서(MUX).dig as structural Verilog
module \_4번_2대1멀티플렉서_MUX  (
  input  X0,
  input  S,
  input  X1,
  output Y
);

  wire and_1_out, and_2_out, not_1_out;

  not not_1 (not_1_out, S);
  and and_1 (and_1_out, X0, not_1_out);
  and and_2 (and_2_out, S, X1);
  or or_1 (Y, and_1_out, and_2_out);
endmodule
