// Digital circuit 5-2번_NAND게이트로OR게이트만들기.dig as structural Verilog
module \_5_2번_NAND게이트로OR게이트만들기  (
  input  A,
  input  B,
  output Y
);

  wire nand_1_out, nand_2_out;

  nand nand_1 (nand_1_out, A, A);
  nand nand_2 (nand_2_out, B, B);
  nand nand_3 (Y, nand_1_out, nand_2_out);
endmodule
