// Digital circuit 6-1번_21세기윤년판독기만들기.dig as structural Verilog
module \_6_1번_21세기윤년판독기만들기  (
  input  A3,
  input  A2,
  input  A1,
  input  A0,
  input  B3,
  input  B2,
  input  B1,
  input  B0,
  output L
);

  wire not_1_out, not_2_out, xor_1_out;

  xor xor_1 (xor_1_out, A0, B1);
  not not_1 (not_1_out, B0);
  not not_2 (not_2_out, xor_1_out);
  and and_1 (L, not_2_out, not_1_out);
endmodule
