// Digital circuit 6-2번_A+B+C를집합의연산으로나타내기.dig as structural Verilog
module \_6_2번_A_B_C를집합의연산으로나타내기  (
  input  A,
  input  B,
  input  C,
  output Y1,
  output Y2,
  output Y3
);

  wire and_1_out, and_2_out, and_3_out, or_1_out, or_3_out;

  or or_1 (or_1_out, A, B);
  and and_1 (and_1_out, A, B);
  and and_2 (and_2_out, B, C);
  and and_3 (and_3_out, C, A);
  or or_2 (Y1, or_1_out, C);
  or or_3 (or_3_out, and_1_out, and_2_out);
  and and_4 (Y3, and_1_out, C);
  or or_4 (Y2, or_3_out, and_3_out);
endmodule
