// Digital circuit 1-1번_반가산기(Half Adder)만들기.dig as structural Verilog
module \_1_1번_반가산기_Half_Adder_만들기  (
  input  P,
  input  Q,
  output S,
  output C_out
);

  xor xor_1 (S, P, Q);
  and and_1 (C_out, P, Q);
endmodule
