// Digital circuit 1-2번_전가산기(Full Adder)만들기.dig as structural Verilog
module \_1_2번_전가산기_Full_Adder_만들기  (
  input  P,
  input  Q,
  input  C_in,
  output S,
  output C_out
);

  wire \_1_1번_반가산기_half_adder_만들기_1_c_out , \_1_1번_반가산기_half_adder_만들기_1_s ,
       \_1_1번_반가산기_half_adder_만들기_2_c_out ;

  \_1_1번_반가산기_Half_Adder_만들기  \_1_1번_반가산기_half_adder_만들기_1  (
    .P(P), .Q(Q), .S(\_1_1번_반가산기_half_adder_만들기_1_s ), .C_out(\_1_1번_반가산기_half_adder_만들기_1_c_out ));
  \_1_1번_반가산기_Half_Adder_만들기  \_1_1번_반가산기_half_adder_만들기_2  (
    .P(\_1_1번_반가산기_half_adder_만들기_1_s ), .Q(C_in), .S(S), .C_out(\_1_1번_반가산기_half_adder_만들기_2_c_out ));
  or or_1 (C_out, \_1_1번_반가산기_half_adder_만들기_1_c_out , \_1_1번_반가산기_half_adder_만들기_2_c_out );
endmodule
