// Digital circuit 1-3번_3비트덧셈연산기만들기.dig as structural Verilog
module \_1_3번_3비트덧셈연산기만들기  (
  input  X2,
  input  Y2,
  input  X1,
  input  Y1,
  input  X0,
  input  Y0,
  output S3,
  output S2,
  output S1,
  output S0
);

  wire \_1_1번_반가산기_half_adder_만들기_1_c_out , \_1_2번_전가산기_full_adder_만들기_1_c_out ;

  \_1_1번_반가산기_Half_Adder_만들기  \_1_1번_반가산기_half_adder_만들기_1  (
    .P(X0), .Q(Y0), .S(S0), .C_out(\_1_1번_반가산기_half_adder_만들기_1_c_out ));
  \_1_2번_전가산기_Full_Adder_만들기  \_1_2번_전가산기_full_adder_만들기_1  (
    .P(X1), .Q(Y1), .C_in(\_1_1번_반가산기_half_adder_만들기_1_c_out ), .S(S1),
    .C_out(\_1_2번_전가산기_full_adder_만들기_1_c_out ));
  \_1_2번_전가산기_Full_Adder_만들기  \_1_2번_전가산기_full_adder_만들기_2  (
    .P(X2), .Q(Y2), .C_in(\_1_2번_전가산기_full_adder_만들기_1_c_out ), .S(S2), .C_out(S3));
endmodule
