// Digital circuit 2-2번_1이상인이진수가2개이상인지판단하기.dig as structural Verilog
module \_2_2번_1이상인이진수가2개이상인지판단하기  (
  input  X1,
  input  X0,
  input  Y1,
  input  Y0,
  input  Z1,
  input  Z0,
  output S0
);

  wire \_2_1번_주어진이진수가1이상인지판단하기_1_s0 , \_2_1번_주어진이진수가1이상인지판단하기_2_s0 , \_2_1번_주어진이진수가1이상인지판단하기_3_s0 ,
       and_1_out, and_2_out, xor_1_out;

  \_2_1번_주어진이진수가1이상인지판단하기  \_2_1번_주어진이진수가1이상인지판단하기_1  (.X1(X1), .X0(X0), .S0(\_2_1번_주어진이진수가1이상인지판단하기_1_s0 ));
  \_2_1번_주어진이진수가1이상인지판단하기  \_2_1번_주어진이진수가1이상인지판단하기_2  (.X1(Y1), .X0(Y0), .S0(\_2_1번_주어진이진수가1이상인지판단하기_2_s0 ));
  \_2_1번_주어진이진수가1이상인지판단하기  \_2_1번_주어진이진수가1이상인지판단하기_3  (.X1(Z1), .X0(Z0), .S0(\_2_1번_주어진이진수가1이상인지판단하기_3_s0 ));
  xor xor_1 (xor_1_out, \_2_1번_주어진이진수가1이상인지판단하기_1_s0 , \_2_1번_주어진이진수가1이상인지판단하기_2_s0 );
  and and_1 (and_1_out, \_2_1번_주어진이진수가1이상인지판단하기_1_s0 , \_2_1번_주어진이진수가1이상인지판단하기_2_s0 );
  and and_2 (and_2_out, xor_1_out, \_2_1번_주어진이진수가1이상인지판단하기_3_s0 );
  or or_1 (S0, and_1_out, and_2_out);
endmodule
