// Digital circuit 3-1번_X^2+Y^2+Z가14이상인지판단하기.dig as structural Verilog
module \_3_1번_X_2_Y_2_Z가14이상인지판단하기  (
  input  X1,
  input  X0,
  input  Y1,
  input  Y0,
  input  Z1,
  input  Z0,
  output S0
);

  wire and_1_out, and_2_out, and_3_out, or_1_out, or_2_out, xor_1_out;

  and and_1 (and_1_out, X1, Y1);
  and and_2 (and_2_out, X0, Y0);
  xor xor_1 (xor_1_out, X0, Y0);
  or or_1 (or_1_out, Z1, Z0);
  and and_3 (and_3_out, xor_1_out, or_1_out);
  or or_2 (or_2_out, and_2_out, and_3_out);
  and and_4 (S0, and_1_out, or_2_out);
endmodule
