// Digital circuit 3-2번_7-segment출력기.dig as structural Verilog
module \_3_2번_7_segment출력기  (
  input  Y,
  output a,
  output b,
  output c,
  output d,
  output e,
  output f,
  output g,
  output dp
);

  not not_1 (a, Y);
  or or_1 (b, Y, a);
  and and_1 (dp, Y, a);
  Seven_Seg seven_seg_1 (.a(a), .b(b), .c(b), .d(Y), .e(a), .f(b), .g(Y), .dp(dp));

  assign c = b;
  assign d = Y;
  assign e = a;
  assign f = b;
  assign g = Y;
endmodule
