// Digital circuit 2번_NOR게이트로AND게이트만들기.dig as structural Verilog
module \_2번_NOR게이트로AND게이트만들기  (
  input  A,
  input  B,
  output Y
);

  wire nor_1_out, nor_2_out;

  nor nor_1 (nor_1_out, A, A);
  nor nor_2 (nor_2_out, B, B);
  nor nor_3 (Y, nor_1_out, nor_2_out);
endmodule
