// Digital circuit 3번_NOR게이트로XOR게이트만들기.dig as structural Verilog
module \_3번_NOR게이트로XOR게이트만들기  (
  input  A,
  input  B,
  output Y
);

  wire nor_1_out, nor_2_out, nor_3_out, nor_4_out;

  nor nor_1 (nor_1_out, A, A);
  nor nor_2 (nor_2_out, B, B);
  nor nor_3 (nor_3_out, A, B);
  nor nor_4 (nor_4_out, nor_1_out, nor_2_out);
  nor nor_5 (Y, nor_4_out, nor_3_out);
endmodule
