// Digital circuit 4번_21세기윤년판독기만들기.dig as structural Verilog
module \_4번_21세기윤년판독기만들기  (
  input  A3,
  input  B3,
  input  A2,
  input  B2,
  input  A1,
  input  B1,
  input  A0,
  input  B0,
  output L
);

  wire and_1_out, and_2_out, nor_1_out, not_1_out, or_1_out;

  not not_1 (not_1_out, B0);
  or or_1 (or_1_out, B1, B0);
  nor nor_1 (nor_1_out, A0, or_1_out);
  and and_1 (and_1_out, B1, not_1_out);
  and and_2 (and_2_out, A0, and_1_out);
  or or_2 (L, nor_1_out, and_2_out);
endmodule
