// Digital circuit B_대피소배정하기.dig as structural Verilog
module \B_대피소배정하기  (
  input  G,
  input  L,
  input  E,
  input  C2,
  input  C1,
  input  C0,
  output Y
);

  wire and_1_out, and_2_out, not_1_out, not_2_out, or_1_out;

  and and_1 (and_1_out, E, C2);
  or or_1 (or_1_out, L, and_1_out);
  not not_1 (not_1_out, E);
  not not_2 (not_2_out, G);
  and and_2 (and_2_out, not_1_out, not_2_out);
  or or_2 (Y, and_2_out, or_1_out);
endmodule
