// Digital circuit C_7segment출력기.dig as structural Verilog
module \C_7segment출력기  (
  input  Y
);

  wire not_1_out, not_2_out, not_3_out, xor_1_out;

  xor xor_1 (xor_1_out, Y, Y);
  not not_1 (not_1_out, xor_1_out);
  not not_2 (not_2_out, Y);
  not not_3 (not_3_out, Y);
  Seven_Seg seven_seg_1 (
    .a(not_2_out), .b(not_3_out), .c(not_1_out), .d(not_1_out), .e(not_1_out), .f(Y), .g(not_1_out),
    .dp(xor_1_out));
endmodule
