// Digital circuit 1번_진리표와bool대수.dig as structural Verilog
module \_1번_진리표와bool대수  (
  input  A,
  input  B,
  output Y
);

  wire xor_1_out;

  xor xor_1 (xor_1_out, A, B);
  not not_1 (Y, xor_1_out);
endmodule
