// Digital circuit 3번_2대1멀티플렉서(MUX).dig as structural Verilog
module \_3번_2대1멀티플렉서_MUX  (
  input  X0,
  input  X1,
  input  S,
  output Y
);

  wire and_1_out, and_2_out, not_1_out;

  not not_1 (not_1_out, S);
  and and_1 (and_1_out, X0, not_1_out);
  and and_2 (and_2_out, X1, S);
  or or_1 (Y, and_1_out, and_2_out);
endmodule
