// Digital circuit A3_3비트덧셈연산기만들기.dig as structural Verilog
module \A3_3비트덧셈연산기만들기  (
  input  X2,
  input  Y2,
  input  X1,
  input  Y1,
  input  X0,
  input  Y0,
  output S3,
  output S2,
  output S1,
  output S0
);

  wire \a1_반가산기_halfadder_만들기_1_c_out , \a2_전가산기_fulladder_만들기_1_c_out ;

  \A1_반가산기_HalfAdder_만들기  \a1_반가산기_halfadder_만들기_1  (.P(X0), .Q(Y0), .S(S0), .C_out(\a1_반가산기_halfadder_만들기_1_c_out ));
  \A2_전가산기_FullAdder_만들기  \a2_전가산기_fulladder_만들기_1  (
    .P(X1), .Q(Y1), .C_in(\a1_반가산기_halfadder_만들기_1_c_out ), .S(S1), .C_out(\a2_전가산기_fulladder_만들기_1_c_out ));
  \A2_전가산기_FullAdder_만들기  \a2_전가산기_fulladder_만들기_2  (
    .P(X2), .Q(Y2), .C_in(\a2_전가산기_fulladder_만들기_1_c_out ), .S(S2), .C_out(S3));
endmodule
