// Digital circuit B_보수계산기만들기.dig as structural Verilog
module \B_보수계산기만들기  (
  input  S3,
  input  S2,
  input  S1,
  input  S0,
  output R2,
  output R1,
  output R0
);

  wire not_1_out, not_2_out, not_3_out, not_4_out;

  not not_1 (not_1_out, S3);
  not not_2 (not_2_out, S2);
  not not_3 (not_3_out, S1);
  not not_4 (not_4_out, S0);
  and and_1 (R2, not_1_out, not_2_out);
  and and_2 (R1, not_1_out, not_3_out);
  and and_3 (R0, not_1_out, not_4_out);
endmodule
