// Digital circuit C_3의나눗셈기만들기.dig as structural Verilog
module \C_3의나눗셈기만들기  (
  input  R2,
  input  R1,
  input  R0,
  output T1,
  output T0
);

  wire and_1_out, and_2_out, and_3_out, not_1_out, or_1_out;

  not not_1 (not_1_out, R2);
  or or_1 (or_1_out, R1, R0);
  and and_1 (and_1_out, R2, R1);
  and and_2 (and_2_out, not_1_out, or_1_out);
  and and_3 (and_3_out, and_1_out, R0);
  or or_2 (T0, and_3_out, and_2_out);

  assign T1 = R2;
endmodule
